// Logisim project ULA.circ as structural Verilog: 4 circuits, main circuit main
module main (
  input  [31:0] Entrada_A,
  input  [31:0] Entrada_B,
  input  [4:0] Seletor,
  output [31:0] \Saída_S ,
  output Overflow
);

  wire Overflow_overflow, undriven;
  wire [4:0] undriven_2;

  OverFlowControler u_Overflow (.Overflow(Overflow_overflow), .Cin(undriven), .in_5(undriven_2));  // open: a, b, s
  CelulaULA celulaula_1 (.a(Entrada_A[30]), .b(Entrada_B[30]), .Cin(1'b0));  // open: Seletor, S, Cout
  CelulaULA celulaula_2 (.a(Entrada_A[31]), .b(Entrada_B[31]));  // open: Cin, Seletor, S, Cout
  CelulaULA celulaula_3 (.a(Entrada_A[28]), .b(Entrada_B[28]));  // open: Cin, Seletor, S, Cout
  CelulaULA celulaula_4 (.a(Entrada_A[29]), .b(Entrada_B[29]));  // open: Cin, Seletor, S, Cout
  CelulaULA celulaula_5 (.a(Entrada_A[26]), .b(Entrada_B[27]));  // open: Cin, Seletor, S, Cout
  CelulaULA celulaula_6 (.a(Entrada_A[27]), .b(Entrada_B[26]));  // open: Cin, Seletor, S, Cout
  CelulaULA celulaula_7 (.a(Entrada_A[24]), .b(Entrada_B[25]));  // open: Cin, Seletor, S, Cout
  CelulaULA celulaula_8 (.a(Entrada_A[25]), .b(Entrada_A[25]));  // open: Cin, Seletor, S, Cout
  CelulaULA celulaula_9 (.a(Entrada_A[22]), .b(Entrada_B[23]));  // open: Cin, Seletor, S, Cout
  CelulaULA celulaula_10 (.a(Entrada_A[23]), .b(Entrada_B[22]));  // open: Cin, Seletor, S, Cout
  CelulaULA celulaula_11 (.a(Entrada_A[20]), .b(Entrada_B[21]));  // open: Cin, Seletor, S, Cout
  CelulaULA celulaula_12 (.a(Entrada_A[21]), .b(Entrada_B[20]));  // open: Cin, Seletor, S, Cout
  CelulaULA celulaula_13 (.a(Entrada_A[18]), .b(Entrada_B[19]));  // open: Cin, Seletor, S, Cout
  CelulaULA celulaula_14 (.a(Entrada_A[19]), .b(Entrada_B[18]));  // open: Cin, Seletor, S, Cout
  CelulaULA celulaula_15 (.a(Entrada_A[16]), .b(Entrada_B[17]));  // open: Cin, Seletor, S, Cout
  CelulaULA celulaula_16 (.a(Entrada_A[17]), .b(Entrada_B[16]));  // open: Cin, Seletor, S, Cout
  CelulaULA celulaula_17 (.a(Entrada_A[14]), .b(Entrada_B[15]));  // open: Cin, Seletor, S, Cout
  CelulaULA celulaula_18 (.a(Entrada_A[15]), .b(Entrada_B[14]));  // open: Cin, Seletor, S, Cout
  CelulaULA celulaula_19 (.a(Entrada_A[12]), .b(Entrada_B[13]));  // open: Cin, Seletor, S, Cout
  CelulaULA celulaula_20 (.a(Entrada_A[13]), .b(Entrada_B[12]));  // open: Cin, Seletor, S, Cout
  CelulaULA celulaula_21 (.a(Entrada_A[10]), .b(Entrada_B[11]));  // open: Cin, Seletor, S, Cout
  CelulaULA celulaula_22 (.a(Entrada_A[11]), .b(Entrada_B[10]), .Cin(Entrada_B[10]));  // open: Seletor, S, Cout
  CelulaULA celulaula_23 (.a(Entrada_A[8]), .b(Entrada_B[9]));  // open: Cin, Seletor, S, Cout
  CelulaULA celulaula_24 (.a(Entrada_A[9]), .b(Entrada_B[8]));  // open: Cin, Seletor, S, Cout
  CelulaULA celulaula_25 (.a(Entrada_A[6]), .b(Entrada_B[7]));  // open: Cin, Seletor, S, Cout
  CelulaULA celulaula_26 (.a(Entrada_A[7]), .b(Entrada_B[6]));  // open: Cin, Seletor, S, Cout
  CelulaULA celulaula_27 (.a(Entrada_A[4]), .b(Entrada_B[5]));  // open: Cin, Seletor, S, Cout
  CelulaULA celulaula_28 (.a(Entrada_A[5]), .b(Entrada_B[4]));  // open: Cin, Seletor, S, Cout
  CelulaULA celulaula_29 (.a(Entrada_A[2]), .b(Entrada_B[3]));  // open: Cin, Seletor, S, Cout
  CelulaULA celulaula_30 (.a(Entrada_A[3]), .b(Entrada_B[2]));  // open: Cin, Seletor, S, Cout
  CelulaULA celulaula_31 (.a(Entrada_A[0]), .b(Entrada_B[1]));  // open: Cin, Seletor, S, Cout
  CelulaULA celulaula_32 (.a(Entrada_A[1]), .b(Entrada_B[0]));  // open: Cin, Seletor, S, Cout

  assign Entrada_B[24] = Entrada_A[25];

  // Notes on the sheet:
  //   00000=AND
  //   00001=OR
  //   00010=XOR
  //   00011=NAND
  //   00100=SOMA INT
  //   00101=SOMA NAT
endmodule

module Somador (
  input  a,
  input  b,
  input  Cin,
  output Cout,
  output s
);

  wire and_1_out, and_2_out, and_3_out, and_4_out, xor_2_out;

  xor xor_1 (s, Cin, xor_2_out);
  xor xor_2 (xor_2_out, a, b);
  and and_1 (and_1_out, ~Cin, a, b);  // AND_Gate
  and and_2 (and_2_out, Cin, ~a, b);  // AND_Gate
  and and_3 (and_3_out, Cin, a, ~b);  // AND_Gate
  and and_4 (and_4_out, Cin, a, b);
  or or_1 (Cout, and_1_out, and_2_out, and_3_out, and_4_out);
endmodule

// Celula
module CelulaULA (
  input  a,
  input  b,
  input  Cin,
  input  [4:0] Seletor,
  output S,
  output Cout
);

  wire and_1_out, nand_1_out, or_1_out, somador_1_s, xor_1_out;

  and and_1 (and_1_out, a, b);
  or or_1 (or_1_out, a, b);
  xor xor_1 (xor_1_out, a, b);
  nand nand_1 (nand_1_out, a, b);
  Somador somador_1 (.Cin(Cin), .a(b), .b(a), .s(somador_1_s), .Cout(Cout));
  Multiplexer #(.select(5), .enable("false")) multiplexer_1 (
    .in0(and_1_out), .in1(or_1_out), .in2(xor_1_out), .in3(nand_1_out), .in4(somador_1_s), .in5(somador_1_s),
    .out(S), .sel(Seletor));  // open: in6, in7, in8, in9, in10, in11, in12, in13, in14, in15, in16, in17, in18, in19, in20, in21, in22, in23, in24, in25, in26, in27, in28, in29, in30, in31

  // Notes on the sheet:
  //   00000=AND
  //   00001=OR
  //   00010=XOR
  //   00011=NAND
  //   00100=SOMA INT
  //   00101=SOMA NAT
endmodule

module OverFlowControler (
  input  Cin,
  input  a,
  input  b,
  input  s,
  input  [4:0] in_5,
  output Overflow
);

  wire and_1_out, and_2_out, and_3_out, or_1_out;

  Multiplexer #(.enable("false")) multiplexer_1 (.in0(Cin), .out(Overflow), .sel(and_1_out));  // open: in1
  and and_1 (and_1_out, in_5[0], ~in_5[1], in_5[2], ~in_5[3], ~in_5[4]);  // AND_Gate
  or or_1 (or_1_out, and_2_out, and_3_out);
  and and_2 (and_2_out, a, b, ~s);  // AND_Gate
  and and_3 (and_3_out, ~a, ~b, s);  // AND_Gate

  // Notes on the sheet:
  //   00100 - Soma de Naturais
  //   00101 - Soma de Inteiros
endmodule
